# Fritzing sketch IkeaMicrowave (saved by Fritzing 0.9.4)
breadboards: 1

parts:
  VCC3 = 4 x AAA Battery Mount
  U2 = ATmega 328P [package=dip]
  Y4 = CRYSTAL [package=hc49us]
  C9 = Capacitor [package=cap-pth-small2]
  C10 = Capacitor [package=cap-pth-small2]
  J9 = Piezo Speaker
  J10 = Piezo Speaker
  R22 = Resistor [tolerance=±5% resistance=1k package="2512 [SMD]"]
  R23 = Resistor [tolerance=±5% resistance=1k package="2512 [SMD]"]
  R24 = Resistor [tolerance=±5% resistance=470 package="2512 [SMD]"]
  RGB_SMD_LED2 = SMD RGB LED (WS2812) [package=5050]
  S6 = Square Pushbutton
  R25 = Resistor [tolerance=±5% resistance=1k package="2512 [SMD]"]
  Q6 = Basic FET N-Channel [package="TO220 [THT]"]
  D2 = P1000K [part_number=P1000K]
  R31 = Resistor [tolerance=±5% resistance=10k package="2512 [SMD]"]
  C14 = Capacitor Polarized [package=cpol-radial-1000uf-25v]

nets:
  N1: VCC3.-, U2.GND#7, R22.Pin_1, R23.Pin_1, S6.leg0, Q6.source, C14.-
  VCC: VCC3.+, U2.VCC, RGB_SMD_LED2.VCC, C14.+
  N2: U2.PD1_(PCINT17/TXD)_[D1], Q6.gate, R31.Pin_0
  N3: U2.PD2_(PCINT18/INT0)_[D2], S6.leg1, R25.Pin_1
  N4: U2.PB6_(PCINT6/XTAL1/TOSC1)_[XTAL1], Y4.2, C10.2
  N5: U2.PB7_(PCINT7/XTAL2/TOSC2)_[XTAL2], Y4.1, C9.1
  N6: U2.PD6_(PCINT22/OC0A/AIN0)_[D6_PWM], J10.pin1
  N7: U2.PD7_(PCINT23/AIN1)_[D7], D2.anode
  N8: U2.PB0_(PCINT0/CLK0/ICP1)_[D8], J9.pin1
  N9: J9.pin2, R23.Pin_0
  N10: J10.pin2, R22.Pin_0
  N11: R24.Pin_0, D2.cathode
  N12: R24.Pin_1, RGB_SMD_LED2.DIn
  N13: RGB_SMD_LED2.VSS, Q6.drain

custom parts:
  ATmega 328P: Atmel ATmega 328P-PU Microcontroller
